# Fritzing sketch BNO085_test (saved by Fritzing 0.9.3b)
breadboards: 1

parts:
  Part1 = Arduino Mega 2560 (Rev3)
  Part2 = Adafruit BNO085 9-DOF Orientation IMU Fusion [part_number="Addfruit #4754"]
  Part3 = Adafruit TCA9548A
  Part4 = Adafruit BNO085 9-DOF Orientation IMU Fusion [part_number="Addfruit #4754"]

nets:
  N1: Part1.D21/SCL, Part3.INPUTSCL
  N2: Part1.D20/SDA, Part3.INPUTSDA
  GND: Part1.GND, Part2.GND, Part3.GND, Part4.GND
  VCC: Part1.5V, Part2.VCC, Part3.VCC, Part4.VCC, Part4.3.3V
  N3: Part2.SCL/SCK/RX, Part3.0SCL
  N4: Part2.SDA/MISO/TX, Part3.0SDA
  N5: Part3.A0, Part3.A1, Part3.A2
  N6: Part3.1SDA, Part4.SDA/MISO/TX, Part4.INT
  N7: Part3.1SCL, Part4.SCL/SCK/RX

custom parts:
  Adafruit TCA9548A: You just found the perfect I2C sensor, and you want to wire up two or three or more of them to your Arduino when you realize "Uh oh, this chip has a fixed I2C address, and from what I know about I2C, you cannot have two devices with the same address on the same SDA/SCL pins!" Are you out of luck? You would be, if you didn't have this ultra-cool TCA9548A 1-to-8 I2C multiplexer! Finally, a way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

// code stored in the sketch: MARG_2.ino
#include <BNO008x>


void setup(){}

void loop(){}
